// Logisim project 8-BIT SIPO SHIFT REGISTER.circ as structural Verilog: 1 circuit, main circuit main
module main (
  input  SI,
  output Q7,
  output Q6,
  output Q5,
  output Q4,
  output Q3,
  output Q2,
  output Q1,
  output Q0
);

  wire CLOCK_out;

  Clock CLOCK (.out(CLOCK_out));
  D_Flip_Flop #(.trigger("falling")) DFF_7 (.clk(CLOCK_out), .D(SI), .Q(Q7));  // open: Qn, preset, en, reset
  D_Flip_Flop #(.trigger("falling")) DFF_6 (.clk(CLOCK_out), .D(Q7), .Q(Q6));  // open: Qn, preset, en, reset
  D_Flip_Flop #(.trigger("falling")) DFF_5 (.clk(CLOCK_out), .D(Q6), .Q(Q5));  // open: Qn, preset, en, reset
  D_Flip_Flop #(.trigger("falling")) DFF_4 (.clk(CLOCK_out), .D(Q5), .Q(Q4));  // open: Qn, preset, en, reset
  D_Flip_Flop #(.trigger("falling")) DFF_3 (.clk(CLOCK_out), .D(Q4), .Q(Q3));  // open: Qn, preset, en, reset
  D_Flip_Flop #(.trigger("falling")) DFF_2 (.clk(CLOCK_out), .D(Q3), .Q(Q2));  // open: Qn, preset, en, reset
  D_Flip_Flop #(.trigger("falling")) DFF_1 (.clk(CLOCK_out), .D(Q2), .Q(Q1));  // open: Qn, preset, en, reset
  D_Flip_Flop #(.trigger("falling")) DFF_0 (.clk(CLOCK_out), .D(Q1), .Q(Q0));  // open: Qn, preset, en, reset

  // Notes on the sheet:
  //   8-BIT SIPO SHIFT REGISTER 
endmodule
